# Fritzing sketch NodeMCU_DHT11_circuit_diagram (saved by Fritzing 0.9.3b)

parts:
  Mod1 = KY-015 Temperature & Humidity Sensor Module [package="Breakout board"]
  U1 = ESP8266 NodeMCU LoLin module

nets:
  N1: Mod1.S, U1.D2
  N2: Mod1.Vin, U1.VU
  N3: Mod1.-, U1.GND

custom parts:
  KY-015 Temperature & Humidity Sensor Module: KY-015 temperature and humidity sensor module, provides a low-latency serial interface to measure humidity and temperature.
  ESP8266 NodeMCU LoLin module: ESP8266 based NodeMCU
